# Fritzing sketch proyecto_test (saved by Fritzing 0.9.3b)
breadboards: 1

parts:
  U1 = ESP8266 WiFi Module [part_number=ESP8266]
  VCC1 = Battery block 9V
  R1 = Resistor [tolerance=±5% resistance=1k package="0603 [SMD]"]
  U4 = BUTTON-MAGNETIC [package=Magnetic-snap]
  U5 = BUTTON-MAGNETIC [package=Magnetic-snap]
  Part1 = Arduino Nano (Rev3.0)

nets:
  N1: U1.RXD, Part1.D1/TX
  VCC: U1.VCC, Part1.3V3
  GND: U1.GND, VCC1.-, Part1.GND
  N2: U1.TXD, Part1.D0/RX
  N3: VCC1.+, U4.1, Part1.VIN
  N4: R1.Pin_0, U5.1
  N5: R1.Pin_1, Part1.D2
